// Logisim project Floating Point Multiplication.circ as structural Verilog: 4 circuits, main circuit main
module main (
);

  wire Clock_out, segment_1_1_p4, segment_2_1_sign_2, Sign1_q, Sign2_q;
  wire [7:0] counter_1_q, Exponent_q, segment_2_1_exponent;
  wire [31:0] A1_q, A2_q, B1_q, B2_q, ram_1_data, rom_1_data, rom_2_data, segment_1_1_p3, segment_1_1_p5,
       segment_2_1_a_out, segment_2_1_b_out, segment_3_1_product;

  Counter counter_1 (.Q(counter_1_q), .clk(Clock_out));  // open: load, D, count, carry, clr
  ROM #(.dataWidth(32)) rom_1 (.addr(counter_1_q), .data(rom_1_data));  // open: sel
  ROM #(.dataWidth(32)) rom_2 (.addr(counter_1_q), .data(rom_2_data));  // open: sel
  Clock Clock (.out(Clock_out));
  // Segment_1 segment_1_1: pin names not known; wires that end beside it: rom_1_data, rom_2_data, segment_1_1_p3, segment_1_1_p4, segment_1_1_p5
  Register #(.width(32)) B1 (.D(segment_1_1_p5), .Q(B1_q), .clk(Clock_out));  // open: en, clr
  Register #(.width(32)) A1 (.D(segment_1_1_p3), .Q(A1_q), .clk(Clock_out));  // open: en, clr
  Register #(.width(1)) Sign1 (.D(segment_1_1_p4), .Q(Sign1_q), .clk(Clock_out));  // open: en, clr
  Segment_2 segment_2_1 (
    .A_IN(A1_q), .B_IN(B1_q), .Sign(Sign1_q), .A_Out(segment_2_1_a_out), .Exponent(segment_2_1_exponent),
    .B_Out(segment_2_1_b_out), .Sign_2(segment_2_1_sign_2));
  Register Exponent (.D(segment_2_1_exponent), .Q(Exponent_q), .clk(Clock_out));  // open: en, clr
  Register #(.width(32)) B2 (.D(segment_2_1_b_out), .Q(B2_q), .clk(Clock_out));  // open: en, clr
  Register #(.width(1)) Sign2 (.D(segment_2_1_sign_2), .Q(Sign2_q), .clk(Clock_out));  // open: en, clr
  Register #(.width(32)) A2 (.D(segment_2_1_a_out), .Q(A2_q), .clk(Clock_out));  // open: en, clr
  Segment_3 segment_3_1 (
    .A_IN(A2_q), .B_IN(B2_q), .Sign(Sign2_q), .Exponent(Exponent_q), .Product(segment_3_1_product));
  RAM #(.dataWidth(32), .bus("separate")) ram_1 (
    .addr(counter_1_q), .din(segment_3_1_product), .data(ram_1_data), .str(1'b1), .clk(Clock_out));  // open: sel, ld, clr

  // Notes on the sheet:
  //   contents of rom_1 (hex, n*v repeats v):
  //   bf333333
  //   contents of rom_2 (hex, n*v repeats v):
  //   43f66000
  //   Pipelined Floating Point Multiplier
  //   22BCE027 - AYUSH PATEL
  //   22BCE018 - ANMOL PANJWANI
endmodule

module Segment_1 (
  input  [31:0] A_IN,
  input  [31:0] B_IN,
  output [31:0] A_Out,
  output Sign_Bit,
  output [31:0] B_Out
);

  xor xor_1 (Sign_Bit, A_IN[31], B_IN[31]);

  assign A_Out = A_IN;
  assign B_Out = B_IN;

  // Notes on the sheet:
  //   Segment -1 : Sign Bit
endmodule

module Segment_2 (
  input  [31:0] A_IN,
  input  [31:0] B_IN,
  input  Sign,
  output [31:0] A_Out,
  output [7:0] Exponent,
  output [31:0] B_Out,
  output Sign_2
);

  wire [7:0] adder_1_out;

  Adder adder_1 (.a(A_IN[30:23]), .b(B_IN[30:23]), .out(adder_1_out));  // open: cin, cout
  Subtractor subtractor_1 (.a(adder_1_out), .b(8'h7f), .out(Exponent));  // open: bin, bout

  assign A_Out = A_IN;
  assign B_Out = B_IN;
  assign Sign_2 = Sign;

  // Notes on the sheet:
  //   Segment - 2 : Exponent Calculation
endmodule

module Segment_3 (
  input  [31:0] A_IN,
  input  [31:0] B_IN,
  input  Sign,
  input  [7:0] Exponent,
  output [31:0] Product
);

  wire [23:0] multiplier_1_cout, multiplier_1_out;

  Multiplier #(.width(24)) multiplier_1 (
    .a({1'b1, A_IN[22:0]}), .b({1'b1, B_IN[22:0]}), .out(multiplier_1_out), .cout(multiplier_1_cout));  // open: cin
  Adder adder_1 (.a(Exponent), .b({8{1'b0}}), .out(Product[30:23]), .cin(multiplier_1_cout[23]));  // open: cout
  Multiplexer #(.width(23), .enable("false")) multiplexer_1 (
    .in0({multiplier_1_cout[21:0], multiplier_1_out[23]}), .in1(multiplier_1_cout[22:0]),
    .out(Product[22:0]), .sel(multiplier_1_cout[23]));

  assign Product[31] = Sign;

  // Notes on the sheet:
  //   Segment - 3 : Mantissa Calculation
endmodule
